# Fritzing sketch picoLayout (saved by Fritzing 0.9.10b)

parts:
  Mod1 = Raspberry Pi Pico
  R1 = Photocell (LDR) [package=THT]
  NEOPIXEL1 = Neopixel Strip -- Black (30/m)

nets:
  N1: Mod1.pin_3, Mod1.pin_23, Mod1.pin_33, Mod1.pin_42, R1.pin_1, NEOPIXEL1.GND
  N2: Mod1.pin_24, R1.pin_0
  N3: Mod1.pin_34, NEOPIXEL1.DI
  N4: Mod1.pin_36, NEOPIXEL1.+5V

notes:
  3V3
  AGND
  GP28_A2
  GND
  GP18
  5V
  Din

custom parts:
  Raspberry Pi Pico: Raspberry Pi Pico. Based around the RP2040 microcontroller the Pico is a low cost microcontroller device bringing Raspberry Pi quality, cost, and easy of use to the microcontroller space. Jan 2021, Split part in to two versions: SMD (this one) and tht. This one is single sided and uses the castellation pads to solder the module to the board (no holes, other than for the USB connector!). The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
  Neopixel Strip -- Black (30/m): Neopixel Strip, Black, 30 pixels per meter.
